# Fritzing sketch votbox (saved by Fritzing 0.9.2b)

parts:
  Matrix_keypad1 = KEYPAD 4x4
  LED1 = smd LED [color="Red (633nm)" package="0805 [SMD]"]
  LED2 = smd LED [color="Green (560nm)" package="0805 [SMD]"]
  R1 = Resistor [tolerance=±5% resistance=220 package=THT]
  R2 = Resistor [tolerance=±5% resistance=220 package=THT]
  J1 = male pin header, 2 pins [form="♂ (male)"]
  J2 = male pin header, 3 pins [form="♂ (male)"]
  J3 = male pin header, 2 pins [form="♂ (male)"]
  D1 = Rectifier Diode [part_number=1N4001 package="300 mil [THT]"]
  R3 = Resistor [tolerance=±5% resistance=1k package=THT]
  U1 = ESP8266 ESP12E WiFi Module [part_number=ESP8266]
  R4 = Resistor [tolerance=±5% resistance=1k package=THT]

nets:
  N1: Matrix_keypad1.col1, J3.pin2, U1.GPIO_0
  N2: Matrix_keypad1.col2, U1.GPIO_2
  N3: Matrix_keypad1.col3, R3.Pin_0, U1.GPIO_15
  N4: Matrix_keypad1.col4, U1.GPIO10
  N5: Matrix_keypad1.row1, U1.GPIO_13
  N6: Matrix_keypad1.row2, U1.GPIO_12
  N7: Matrix_keypad1.row3, U1.GPIO_14
  N8: Matrix_keypad1.row4, U1.GPIO_16
  N9: LED1.cathode, R1.Pin_0
  N10: LED1.anode, U1.GPIO_4
  N11: LED2.cathode, R2.Pin_1
  N12: LED2.anode, U1.GPIO_5
  N13: R1.Pin_1, R2.Pin_0, J1.pin1, J3.pin1
  N14: J1.pin2, D1.anode
  N15: J2.pin1, U1.TXD
  N16: J2.pin2, R3.Pin_1, U1.GND
  N17: J2.pin3, U1.RXD
  N18: D1.cathode, U1.VCC, R4.Pin_0
  N19: U1.CH_PD, R4.Pin_1

notes:
  TX
  GND
  RX
  Prog
  VCC 3.7V

custom parts:
  KEYPAD 4x4: Matrix keypad 16 buttons, 4 rows x 4 columns
  ESP8266 ESP12E WiFi Module: Generic WiFi Module based on the ESP8266 with onboard PCB antenna and UART communications
